# Fritzing sketch SimonSaysUltraAlpha (saved by Fritzing 0.7.10b)
breadboards: 1

parts:
  100_Ohms = Resistor [tolerance=±5% resistance=100 package=THT]
  Buzzer = Piezo Speaker
  Arduino1 = Arduino
  S1 = Pushbutton [package="[THT]"]
  S2 = Pushbutton [package="[THT]"]
  100_Ohms1 = Resistor [tolerance=±5% resistance=10k package=THT]
  10k_Ohms2 = Resistor [tolerance=±5% resistance=10k package=THT]

nets:
  N1: 100_Ohms.Pin_0, Arduino1.D11
  N2: 100_Ohms.Pin_1, Buzzer.pin1, Buzzer.pin2, Arduino1.GND, 100_Ohms1.Pin_0, 10k_Ohms2.Pin_1
  N3: Arduino1.D3, S2.Pin_1, S2.Pin_2, 100_Ohms1.Pin_1
  N4: Arduino1.D2, S1.Pin_1, S1.Pin_2, 10k_Ohms2.Pin_0
  N5: Arduino1.+5V, S1.Pin_3, S1.Pin_4, S2.Pin_3, S2.Pin_4
