# Fritzing sketch SimonSaysUltraAlpha (saved by Fritzing 0.7.10b)
breadboards: 1

parts:
  Arduino1 = Arduino
  100_Ohms1 = Resistor [tolerance=±5% resistance=10k package=THT]
  Buzzer = Piezo Speaker
  S2 = Pushbutton [package="[THT]"]
  10k_Ohms2 = Resistor [tolerance=±5% resistance=10k package=THT]
  100_Ohms2 = Resistor [tolerance=±5% resistance=10k package=THT]
  S3 = Pushbutton [package="[THT]"]
  S4 = Pushbutton [package="[THT]"]
  10k_Ohms3 = Resistor [tolerance=±5% resistance=10k package=THT]
  100_Ohms = Resistor [tolerance=±5% resistance=100 package=THT]
  S1 = Pushbutton [package="[THT]"]

nets:
  N1: Arduino1.GND, Arduino1.D2, Buzzer.pin1, 10k_Ohms2.Pin_0, S1.Pin_1, S1.Pin_2
  N2: Arduino1.D11, 100_Ohms.Pin_0
  N3: Arduino1.D5, Arduino1.+5V, S4.Pin_3, S4.Pin_4
  N4: Arduino1.D4, S3.Pin_1, S3.Pin_2, 10k_Ohms3.Pin_0
  N5: Arduino1.D3, 100_Ohms1.Pin_0, S2.Pin_1, S2.Pin_2
  N6: Buzzer.pin2, 100_Ohms.Pin_1
  N7: S2.Pin_3, S2.Pin_4
  N8: 100_Ohms2.Pin_0, S4.Pin_1, S4.Pin_2
  N9: S3.Pin_3, S3.Pin_4
  N10: S1.Pin_3, S1.Pin_4
